# Fritzing sketch chessLogger (saved by Fritzing 0.9.3b)
breadboards: 2

parts:
  Part1 = Arduino Mega 2560 (Rev3)
  S1 = SWITCH-MOMENTARY-2 [package=reed_switch_plastic]
  S2 = SWITCH-MOMENTARY-2 [package=reed_switch_plastic]
  S3 = SWITCH-MOMENTARY-2 [package=reed_switch_plastic]
  S4 = SWITCH-MOMENTARY-2 [package=reed_switch_plastic]
  S5 = SWITCH-MOMENTARY-2 [package=reed_switch_plastic]
  S6 = SWITCH-MOMENTARY-2 [package=reed_switch_plastic]
  S7 = SWITCH-MOMENTARY-2 [package=reed_switch_plastic]
  S8 = SWITCH-MOMENTARY-2 [package=reed_switch_plastic]
  S9 = SWITCH-MOMENTARY-2 [package=reed_switch_plastic]
  S10 = SWITCH-MOMENTARY-2 [package=reed_switch_plastic]
  S11 = SWITCH-MOMENTARY-2 [package=reed_switch_plastic]
  S12 = SWITCH-MOMENTARY-2 [package=reed_switch_plastic]
  S13 = SWITCH-MOMENTARY-2 [package=reed_switch_plastic]
  S14 = SWITCH-MOMENTARY-2 [package=reed_switch_plastic]
  S15 = SWITCH-MOMENTARY-2 [package=reed_switch_plastic]
  S16 = SWITCH-MOMENTARY-2 [package=reed_switch_plastic]
  S17 = SWITCH-MOMENTARY-2 [package=reed_switch_plastic]
  S18 = SWITCH-MOMENTARY-2 [package=reed_switch_plastic]
  S19 = SWITCH-MOMENTARY-2 [package=reed_switch_plastic]
  S20 = SWITCH-MOMENTARY-2 [package=reed_switch_plastic]
  S21 = SWITCH-MOMENTARY-2 [package=reed_switch_plastic]
  S22 = SWITCH-MOMENTARY-2 [package=reed_switch_plastic]
  S23 = SWITCH-MOMENTARY-2 [package=reed_switch_plastic]
  S24 = SWITCH-MOMENTARY-2 [package=reed_switch_plastic]
  S25 = SWITCH-MOMENTARY-2 [package=reed_switch_plastic]
  S26 = SWITCH-MOMENTARY-2 [package=reed_switch_plastic]
  S27 = SWITCH-MOMENTARY-2 [package=reed_switch_plastic]
  S28 = SWITCH-MOMENTARY-2 [package=reed_switch_plastic]
  S29 = SWITCH-MOMENTARY-2 [package=reed_switch_plastic]
  S30 = SWITCH-MOMENTARY-2 [package=reed_switch_plastic]
  S31 = SWITCH-MOMENTARY-2 [package=reed_switch_plastic]
  S32 = SWITCH-MOMENTARY-2 [package=reed_switch_plastic]
  S33 = SWITCH-MOMENTARY-2 [package=reed_switch_plastic]
  S34 = SWITCH-MOMENTARY-2 [package=reed_switch_plastic]
  S35 = SWITCH-MOMENTARY-2 [package=reed_switch_plastic]
  S36 = SWITCH-MOMENTARY-2 [package=reed_switch_plastic]
  S37 = SWITCH-MOMENTARY-2 [package=reed_switch_plastic]
  S38 = SWITCH-MOMENTARY-2 [package=reed_switch_plastic]
  S39 = SWITCH-MOMENTARY-2 [package=reed_switch_plastic]
  S40 = SWITCH-MOMENTARY-2 [package=reed_switch_plastic]
  S41 = SWITCH-MOMENTARY-2 [package=reed_switch_plastic]
  S42 = SWITCH-MOMENTARY-2 [package=reed_switch_plastic]
  S43 = SWITCH-MOMENTARY-2 [package=reed_switch_plastic]
  S44 = SWITCH-MOMENTARY-2 [package=reed_switch_plastic]
  S45 = SWITCH-MOMENTARY-2 [package=reed_switch_plastic]
  S46 = SWITCH-MOMENTARY-2 [package=reed_switch_plastic]
  S47 = SWITCH-MOMENTARY-2 [package=reed_switch_plastic]
  S48 = SWITCH-MOMENTARY-2 [package=reed_switch_plastic]
  S49 = SWITCH-MOMENTARY-2 [package=reed_switch_plastic]
  S50 = SWITCH-MOMENTARY-2 [package=reed_switch_plastic]
  S51 = SWITCH-MOMENTARY-2 [package=reed_switch_plastic]
  S52 = SWITCH-MOMENTARY-2 [package=reed_switch_plastic]
  S53 = SWITCH-MOMENTARY-2 [package=reed_switch_plastic]
  S54 = SWITCH-MOMENTARY-2 [package=reed_switch_plastic]
  S55 = SWITCH-MOMENTARY-2 [package=reed_switch_plastic]
  S56 = SWITCH-MOMENTARY-2 [package=reed_switch_plastic]
  S57 = SWITCH-MOMENTARY-2 [package=reed_switch_plastic]
  S58 = SWITCH-MOMENTARY-2 [package=reed_switch_plastic]
  S59 = SWITCH-MOMENTARY-2 [package=reed_switch_plastic]
  S60 = SWITCH-MOMENTARY-2 [package=reed_switch_plastic]
  S61 = SWITCH-MOMENTARY-2 [package=reed_switch_plastic]
  S62 = SWITCH-MOMENTARY-2 [package=reed_switch_plastic]
  S63 = SWITCH-MOMENTARY-2 [package=reed_switch_plastic]
  S64 = SWITCH-MOMENTARY-2 [package=reed_switch_plastic]
  U1 = NodeMCU V1.0
  Piece_Selection = Momentary Switch [package=ksa_sealed_tac_switch]
  Cancel_Reset_Check_Mate = Momentary Switch [package=ksa_sealed_tac_switch]

nets:
  N1: Part1.A8, S10.2
  N2: Part1.A9, S12.2
  N3: Part1.A10, S11.2
  N4: Part1.A11, S9.2
  N5: Part1.A12, S14.2
  N6: Part1.A13, S16.2
  N7: Part1.A14, S15.2
  N8: Part1.A15, S13.2
  N9: Part1.A0, S1.2
  N10: Part1.A1, S2.2
  N11: Part1.A2, S3.2
  N12: Part1.A3, S4.2
  N13: Part1.A4, S6.2
  N14: Part1.A5, S8.2
  N15: Part1.A6, S7.2
  N16: Part1.A7, S5.2
  N17: Part1.D21/SCL, Piece_Selection.2
  N18: Part1.D20/SDA, Cancel_Reset_Check_Mate.4
  N19: Part1.D19/RX1, S45.1
  N20: Part1.D18/TX1, S47.1
  N21: Part1.D17_PWM/RX2, S48.1
  N22: Part1.D16_PWM/TX2, S46.1
  N23: Part1.D15/RX3, U1.TX
  N24: Part1.D14/TX3, U1.RX
  N25: Part1.D13_PWM, S34.1
  N26: Part1.D12_PWM, S36.1
  N27: Part1.D11_PWM, S35.1
  N28: Part1.D10_PWM, S33.1
  N29: Part1.D9_PWM, S38.1
  N30: Part1.D8_PWM, S40.1
  5V: Part1.5V, U1.Vin
  GND: Part1.GND, S1.1, S2.1, S3.1, S4.1, S5.1, S6.1, S7.1, S8.1, S9.1, S10.1, S11.1, S12.1, S13.1, S14.1, S15.1, S16.1, S17.1, S18.1, S19.1, S20.1, S21.1, S22.1, S23.1, S24.1, S25.1, S26.1, S27.1, S28.1, S29.1, S30.1, S31.1, S32.1, U1.GND
  N31: Part1.D2_PWM, S41.1
  N32: Part1.D3_PWM, S43.1
  N33: Part1.D4_PWM, S44.1
  N34: Part1.D5_PWM, S42.1
  N35: Part1.D6_PWM, S37.1
  N36: Part1.D7_PWM, S39.1
  N37: Part1.D22, S50.1
  N38: Part1.D23, S52.1
  N39: Part1.D24, S51.1
  N40: Part1.D25, S49.1
  N41: Part1.D26, S54.1
  N42: Part1.D27, S56.1
  N43: Part1.D28, S55.1
  N44: Part1.D29, S53.1
  N45: Part1.D30, S58.1
  N46: Part1.D31, S60.1
  N47: Part1.D32, S59.1
  N48: Part1.D33, S57.1
  N49: Part1.D34, S62.1
  N50: Part1.D35, S64.1
  N51: Part1.D36, S63.1
  N52: Part1.D37, S61.1
  N53: Part1.D38, S31.2
  N54: Part1.D39, S29.2
  N55: Part1.D40, S32.2
  N56: Part1.D41, S30.2
  N57: Part1.D42, S25.2
  N58: Part1.D43, S27.2
  N59: Part1.D44, S28.2
  N60: Part1.D45, S26.2
  N61: Part1.D46, S21.2
  N62: Part1.D47, S23.2
  N63: Part1.D48, S22.2
  N64: Part1.D49, S24.2
  N65: Part1.D50, S17.2
  N66: Part1.D51, S19.2
  N67: Part1.D52, S18.2
  N68: Part1.D53, S20.2
  N69: S33.2, S34.2, S35.2, S36.2, S37.2, S38.2, S39.2, S40.2, S41.2, S42.2, S43.2, S44.2, S45.2, S46.2, S47.2, S48.2, S49.2, S50.2, S51.2, S52.2, S53.2, S54.2, S55.2, S56.2, S57.2, S58.2, S59.2, S60.2, S61.2, S62.2, S63.2, S64.2, Piece_Selection.3, Cancel_Reset_Check_Mate.1

custom parts:
  NodeMCU V1.0: ESP8266 based NodeMCU
